// Logisim project ALU.circ as structural Verilog: 7 circuits, main circuit Multiplication
module ALU (
  input  [31:0] Data_A,
  input  [31:0] Data_B,
  input  [3:0] Selector,
  output [31:0] ALU_Output,
  output [31:0] High,
  output Zero_Flag,
  output Negative_Flag
);

  wire slt_bit, sltu_bit;
  wire [31:0] Add, And, DivHigh, DivLow, DivuHigh, DivuLow, MultHigh, MultLow, MuluHigh, MuluLow, Nor, Or,
       slt, sltu, Sub, Xor;

  Adder #(.width(32)) adder_1 (.a(Data_A), .b(Data_B), .out(Add));  // open: cin, cout
  Multiplier #(.width(32)) multiplier_1 (.a(Data_A), .b(Data_B), .out(MuluLow), .cout(MuluHigh));  // open: cin
  Comparator #(.width(32)) comparator_1 (.a(Data_A), .b(Data_B), .lt(slt_bit));  // open: gt, eq
  assign slt = {{31{1'b0}}, slt_bit};  // Bit_Extender bit_extender_1
  Multiplication multiplication_1 (.A(Data_A), .B(Data_B), .Low(MultLow), .High(MultHigh));
  Subtractor #(.width(32)) subtractor_1 (.a(Data_A), .b(Data_B), .out(Sub));  // open: bin, bout
  Divider #(.width(32)) divider_1 (.a(Data_A), .b(Data_B), .out(DivuLow), .rem(DivuHigh));  // open: upper
  Division division_1 (.A(Data_A), .B(Data_B), .Low(DivLow), .High(DivHigh));
  Comparator #(.width(32), .mode("unsigned")) comparator_2 (.a(Data_A), .b(Data_B), .lt(sltu_bit));  // open: gt, eq
  assign sltu = {{31{1'b0}}, sltu_bit};  // Bit_Extender bit_extender_2
  Multiplexer #(.select(4), .width(32), .enable("false")) multiplexer_1 (
    .in0(Add), .in1(Sub), .in2(slt), .in3(sltu), .in4(And), .in5(Or), .in6(Nor), .in7(Xor), .in8(MultLow),
    .in9(MuluLow), .in10(DivLow), .in11(DivuLow), .out(ALU_Output), .sel(Selector));  // open: in12, in13, in14, in15
  Multiplexer #(.select(2), .width(32), .enable("false")) multiplexer_2 (
    .in0(MultHigh), .in1(MuluHigh), .in2(DivHigh), .in3(DivuHigh), .out(High), .sel(Selector[1:0]));
  assign And = Data_A & Data_B;  // AND_Gate and_1, 32 bits wide
  assign Or = Data_A | Data_B;  // OR_Gate or_1, 32 bits wide
  Comparator #(.width(32)) comparator_3 (
    .a(ALU_Output), .b({32{1'b0}}), .eq(Zero_Flag), .lt(Negative_Flag));  // open: gt
  assign Nor = ~(Data_A | Data_B);  // NOR_Gate nor_1, 32 bits wide
  assign Xor = Data_A ^ Data_B;  // XOR_Gate xor_1, 32 bits wide

  // Other names for the same wires on the sheet: A[31:0] = Data_A; B[31:0] = Data_B; Output[31:0] = ALU_Output;
  //   SelectorHigh[1:0] = Selector[1:0]

  // Notes on the sheet:
  //   INPUTS
  //   ARITHMETIC
  //   LOGIC
  //   OUTPUTS
endmodule

module Multiplication (
  input  [31:0] A,
  input  [31:0] B,
  output [31:0] Low,
  output [31:0] High
);

  wire negative_1_carryout, NegOut, signA, signB;
  wire [31:0] adder_1_out, multiplier_1_cout, multiplier_1_out, negative_1_output,
       negative_to_positive_1_output, negative_to_positive_2_output, not_1_out;

  // Probe on A
  // Probe on B
  Negative_To_Positive negative_to_positive_1 (.A(A), .Output(negative_to_positive_1_output), .Negative(signA));
  Negative_To_Positive negative_to_positive_2 (.A(B), .Output(negative_to_positive_2_output), .Negative(signB));
  Multiplier #(.width(32)) multiplier_1 (
    .a(negative_to_positive_1_output), .b(negative_to_positive_2_output), .out(multiplier_1_out),
    .cout(multiplier_1_cout));  // open: cin
  xor xor_1 (NegOut, signA, signB);
  assign not_1_out = ~multiplier_1_cout;  // NOT_Gate not_1, 32 bits wide
  Negative negative_1 (.A(multiplier_1_out), .Output(negative_1_output), .CarryOut(negative_1_carryout));
  Adder #(.width(32)) adder_1 (
    .a(not_1_out), .b({32{1'b0}}), .out(adder_1_out), .cin(negative_1_carryout));  // open: cout
  // Probe on Low
  Multiplexer #(.width(32), .enable("false")) multiplexer_1 (
    .in0(multiplier_1_out), .in1(negative_1_output), .out(Low), .sel(NegOut));
  Multiplexer #(.width(32), .enable("false")) multiplexer_2 (
    .in0(multiplier_1_cout), .in1(adder_1_out), .out(High), .sel(NegOut));
  // Probe on High
endmodule

module Division (
  input  [31:0] A,
  input  [31:0] B,
  output [31:0] Low,
  output [31:0] High
);

  wire NegOut, selectorA, selectorB;
  wire [31:0] divider_1_out, divider_1_rem, negative_1_output, negative_2_output,
       negative_to_positive_1_output, negative_to_positive_2_output;

  // Probe on A
  // Probe on B
  Negative_To_Positive negative_to_positive_1 (.A(A), .Output(negative_to_positive_1_output), .Negative(selectorA));
  Negative_To_Positive negative_to_positive_2 (.A(B), .Output(negative_to_positive_2_output), .Negative(selectorB));
  Divider #(.width(32)) divider_1 (
    .a(negative_to_positive_1_output), .b(negative_to_positive_2_output), .out(divider_1_out),
    .rem(divider_1_rem));  // open: upper
  xor xor_1 (NegOut, selectorA, selectorB);
  Negative negative_1 (.A(divider_1_out), .Output(negative_1_output));  // open: CarryOut
  Negative negative_2 (.A(divider_1_rem), .Output(negative_2_output));  // open: CarryOut
  Multiplexer #(.width(32), .enable("false")) multiplexer_1 (
    .in0(divider_1_out), .in1(negative_1_output), .out(Low), .sel(NegOut));
  Multiplexer #(.width(32), .enable("false")) multiplexer_2 (
    .in0(divider_1_rem), .in1(negative_2_output), .out(High), .sel(NegOut));
  // Probe on Low
  // Probe on High
endmodule

module ConstExtender (
  input  in_1,
  input  [15:0] in_2,
  output [31:0] out_3
);

  wire and_1_out;

  and and_1 (and_1_out, ~in_1, in_2[15]);  // AND_Gate
  assign out_3 = {{16{and_1_out}}, in_2};  // Bit_Extender bit_extender_1

  // Other names for the same wires on the sheet: const[15:0] = in_2; I15 = in_2[15]; Output[31:0] = out_3;
  //   Selector = in_1
endmodule

module Negative_To_Positive (
  input  [31:0] A,
  output [31:0] Output,
  output Negative
);

  wire [31:0] negative_1_output;

  // Probe on A
  Negative negative_1 (.A(A), .Output(negative_1_output));  // open: CarryOut
  Multiplexer #(.width(32), .enable("false")) multiplexer_1 (
    .in0(A), .in1(negative_1_output), .out(Output), .sel(A[31]));
  // Probe on Output

  assign Negative = A[31];
endmodule

module Negative (
  input  [31:0] A,
  output [31:0] Output,
  output CarryOut
);

  wire [31:0] not_1_out;

  // Probe on A
  assign not_1_out = ~A;  // NOT_Gate not_1, 32 bits wide
  Adder #(.width(32)) adder_1 (.a(not_1_out), .b(32'h1), .out(Output), .cout(CarryOut));  // open: cin
  // Probe on Output
endmodule

module ALU_Input (
  input  [31:0] Rt,
  input  [15:0] Const,
  input  Const_Extender_Selector,
  input  Type_I,
  input  [1:0] BC_Pre_Input_Selector,
  input  [3:0] Operation_Selector,
  output [31:0] Output,
  output [3:0] Operation_Selector_2
);

  wire or_1_out;
  wire [31:0] Const_t, multiplexer_1_out;

  ConstExtender constextender_1 (.in_2(Const), .out_3(Const_t), .in_1(Const_Extender_Selector));
  or or_1 (or_1_out, ~Type_I, BC_Pre_Input_Selector[0]);  // OR_Gate
  Multiplexer #(.width(32), .enable("false")) multiplexer_1 (
    .in0(Const_t), .in1(Rt), .out(multiplexer_1_out), .sel(or_1_out));
  Multiplexer #(.width(32), .enable("false")) multiplexer_2 (
    .in0(multiplexer_1_out), .in1({32{1'b0}}), .out(Output), .sel(BC_Pre_Input_Selector[1]));
  Multiplexer #(.width(4), .enable("false")) multiplexer_3 (
    .in0(Operation_Selector), .in1(4'b0001), .out(Operation_Selector_2), .sel(BC_Pre_Input_Selector[0]));

  // Other names for the same wires on the sheet: No_beq_bne = BC_Pre_Input_Selector[1]
endmodule
