// Logisim project Branch Control.circ as structural Verilog: 1 circuit, main circuit Branch-Control
module Branch_Control (
  input  [31:0] Rs,
  input  [31:0] Rt,
  input  [31:0] PC_out,
  input  [25:0] destination,
  input  [1:0] Selector,
  input  [15:0] offset,
  input  [2:0] Flag_Condition,
  output [31:0] PC_in
);

  wire comparator_2_eq, multiplexer_1_out, Rs_0, Rs_0_t, Rs__0, Rs__Rt, Rs__Rt_t;
  wire [13:0] bit_extender_1_out;
  wire [31:0] multiplexer_2_out, PC_4, PC_4_x;

  Adder #(.width(32)) adder_1 (.a(PC_out), .b(32'h4), .out(PC_4));  // open: cin, cout
  assign bit_extender_1_out = {{13{offset[15]}}, offset[15]};  // Bit_Extender bit_extender_1
  Adder #(.width(32)) adder_2 (.a(PC_4), .b({bit_extender_1_out, offset, 2'b00}), .out(PC_4_x));  // open: cin, cout
  Comparator #(.width(32)) comparator_1 (.a(Rs), .b(Rt), .eq(Rs__Rt_t));  // open: gt, lt
  Comparator #(.width(32)) comparator_2 (.a(Rs), .b({32{1'b0}}), .gt(Rs_0_t), .eq(comparator_2_eq), .lt(Rs_0));
  not not_1 (Rs__Rt, Rs__Rt_t);
  or or_1 (Rs__0, comparator_2_eq, Rs_0);
  Multiplexer #(.select(3), .enable("false")) multiplexer_1 (
    .in0(Rs__Rt_t), .in1(Rs__Rt), .in2(Rs_0_t), .in3(Rs__0), .in4(Rs_0), .out(multiplexer_1_out),
    .sel(Flag_Condition));  // open: in5, in6, in7
  Multiplexer #(.width(32), .enable("false")) multiplexer_2 (
    .in0(PC_4), .in1(PC_4_x), .out(multiplexer_2_out), .sel(multiplexer_1_out));
  Multiplexer #(.select(2), .width(32), .enable("false")) multiplexer_3 (
    .in0(multiplexer_2_out), .in1(multiplexer_2_out), .in2({PC_out[31:28], destination, 2'b00}), .in3(Rs),
    .out(PC_in), .sel(Selector));

  // Other names for the same wires on the sheet: FlagCondition[2:0] = Flag_Condition; dest[25:0] = destination;
  //   jmp[31:2] = {PC_out[31:28], destination}; PC[31:0] = PC_out

  // Notes on the sheet:
  //   Branch Control
endmodule
