// Logisim project Branch-Control-Selector.circ as structural Verilog: 1 circuit, main circuit Branch-Control-Pre-Selector
module Branch_Control_Pre_Selector (
  input  in_1,
  input  in_2,
  output Pre_Selector
);

  or or_1 (Pre_Selector, in_1, in_2);

  // Other names for the same wires on the sheet: beq = in_1; bne = in_2
endmodule
