// Logisim project Control Unit.circ as structural Verilog: 1 circuit, main circuit main
module main (
  input  clock,
  input  start,
  input  reset,
  input  is_tty,
  input  is_ALU,
  input  is_save,
  input  is_jump,
  input  is_read,
  input  is_write,
  input  ready_read,
  input  ready_write,
  output get_data,
  output write_data,
  output PC_enable,
  output RF_enable,
  output Inst__Memory_enable,
  output tty_enable,
  output kbd_enable,
  output \end 
);

  wire clk, demultiplexer_1_out0, demultiplexer_1_out1, demultiplexer_2_out0, demultiplexer_2_out1,
       Fetch_instruction_q, Idle_q, MEM, next_inst, or_3_out, SAVE, Save_q;
  wire [1:0] exe_select;

  Clock clock_1 (.out(clk));
  or or_1 (SAVE, is_ALU, is_save);
  or or_2 (MEM, is_write, is_read);
  or or_3 (or_3_out, demultiplexer_1_out0, reset);
  D_Flip_Flop Idle (.clk(clk), .D(or_3_out), .Q(Idle_q));  // open: Qn, preset, en, reset
  Demultiplexer #(.enable("false")) demultiplexer_1 (
    .out0(demultiplexer_1_out0), .out1(demultiplexer_1_out1), .in(Idle_q), .sel(start));
  D_Flip_Flop u_Save (.clk(clk), .D(RF_enable), .Q(Save_q));  // open: Qn, preset, en, reset
  or or_4 (get_data, demultiplexer_2_out0, next_inst, demultiplexer_1_out1);
  Priority_Encoder #(.select(2)) priority_encoder_1 (
    .in0(SAVE), .in1(MEM), .in2(is_jump), .in3(is_tty), .out(exe_select), .en_in(1'b1));  // open: gs, en_out
  D_Flip_Flop Fetch_instruction (.clk(clk), .D(get_data), .Q(Fetch_instruction_q));  // open: Qn, preset, en, reset
  Demultiplexer #(.enable("false")) demultiplexer_2 (
    .out0(demultiplexer_2_out0), .out1(demultiplexer_2_out1), .in(Fetch_instruction_q), .sel(ready_read));
  Demultiplexer #(.select(2), .enable("false")) demultiplexer_3 (
    .out0(RF_enable), .out1(MEM), .out2(is_jump), .out3(is_tty), .in(demultiplexer_2_out1), .sel(exe_select));

  assign Inst__Memory_enable = get_data;

  // Other names for the same wires on the sheet: IM_en = get_data; PC_en = PC_enable; ready_r = ready_read;
  //   ready_w = ready_write; RF_en = RF_enable; save_t = RF_enable; tty_en = tty_enable

  // Notes on the sheet:
  //   Outputs
  //   Inputs
endmodule
