// Logisim project Data-Path.circ as structural Verilog: 1 circuit, main circuit main
module main (
  input  [6:0] Keyboard,
  input  [31:0] RAM_data,
  input  [15:0] constante,
  input  Enable_Hi_Lo,
  input  [4:0] Data_Adress,
  input  R_W,
  input  [4:0] Selector_A,
  input  store_word,
  input  [4:0] Selector_B,
  input  KBD_AVAILABLE,
  input  [2:0] RF_input_selector,
  input  Type_I,
  input  [3:0] ALU_Op__Selector,
  input  Reset,
  input  Const_extender_selector,
  input  Clock,
  input  HI_LO_enable,
  output [6:0] tty_DATA,
  output [31:0] RAM_write_data,
  output [31:0] RS,
  output [31:0] RT
);

  wire [31:0] alu_input_1_b, ALU_out, High_in, High_out, Low_out, main_1_rf_input, SP;

  ALU_Input alu_input_1 (
    .RT(RT), .Const(constante), .B(alu_input_1_b), .Const_Extender_Selector(Const_extender_selector),
    .Type_I(Type_I));
  Register_File_Input_main main_1 (
    .RAM(RAM_data), .ALU_Output(ALU_out), .Keyboard(Keyboard), .High(High_out),
    .KBD_available(KBD_AVAILABLE), .Low(Low_out), .RF_Input(main_1_rf_input), .Selector(RF_input_selector),
    .clock(Clock));
  // ALU alu_1: pin names not known; wires that end beside it: RS, alu_input_1_b, ALU_Op__Selector, ALU_out, High_in
  Multiplexer #(.width(32), .enable("false")) multiplexer_1 (
    .in0(RS), .in1(RT), .out(RAM_write_data), .sel(store_word));
  // Register_File_main main_2: pin names not known; wires that end beside it: R_W, main_1_rf_input, R_W, Data_Adress, Clock, Selector_A, Selector_B, Reset, RS, RT, SP
  HI_LO_main main_3 (
    .Hi_Lo_enable(HI_LO_enable), .Clock(Clock), .High_in(High_in), .Low_in(ALU_out), .Low_out(Low_out),
    .High_out(High_out));

  assign tty_DATA = RS[6:0];

  // Other names for the same wires on the sheet: CES = Const_extender_selector; Clk = Clock; const[15:0] = constante;
  //   DA[4:0] = Data_Adress; E_HL = Enable_Hi_Lo; HI_LO_en = HI_LO_enable; KBD_AVAIL = KBD_AVAILABLE;
  //   Kbd_data[6:0] = Keyboard; op[3:0] = ALU_Op__Selector; RAM__w[31:0] = RAM_write_data; RAM_d[31:0] = RAM_data;
  //   RF_sel[2:0] = RF_input_selector; Rst = Reset; SA[4:0] = Selector_A; SB[4:0] = Selector_B; sw = store_word

  // Notes on the sheet:
  //   Inputs
  //   Outputs
endmodule
